# Fritzing sketch Diagram (saved by Fritzing 0.8.7b)
breadboards: 1

parts:
  LCD1 = LCD screen
  R1 = Rotary Potentiometer (Small) [maximum_resistance=100kΩ package=THT]
  Part1 = Arduino Uno (Rev3)
  Real_Time_Clock = mystery part, 4 pins [chip_label=RTC]
  T1 = LM35 Temperature Sensor [package="TO92 [THT]"]
  R2 = Resistor [tolerance=±5% resistance=4.7k package=THT]
  Relay = mystery part, 6 pins [chip_label=Relay]

nets:
  GND: LCD1.VSS, LCD1.R/W, R1.leg1, Part1.GND, Real_Time_Clock.pin4, T1.GND, Relay.pin6
  VDD: LCD1.VDD, R1.leg2, Part1.5V, Real_Time_Clock.pin3, T1.+Vs, R2.Pin_1, Relay.pin4
  N1: LCD1.V0, R1.wiper
  N2: LCD1.RS, Part1.D12/MISO
  N3: LCD1.E, Part1.D11_PWM/MOSI
  N4: LCD1.DB4, Part1.D5_PWM
  N5: LCD1.DB5, Part1.D4
  N6: LCD1.DB6, Part1.D3_PWM
  N7: LCD1.DB7, Part1.D2
  N8: Part1.A4/SDA, Real_Time_Clock.pin2
  N9: Part1.A5/SCL, Real_Time_Clock.pin1
  N10: Part1.D13/SCK, Relay.pin5
  N11: Part1.D7, T1.Vout, R2.Pin_0
